// Logisim project S2_T3_Logisim.circ as structural Verilog: 10 circuits, main circuit main
module main (
  input  in_1,
  input  START,
  input  RESET,
  input  Submit,
  input  A4,
  input  A3,
  input  A2,
  input  A1,
  input  A0,
  output C3,
  output C2,
  output C1,
  output C0,
  output D3,
  output D2,
  output D1,
  output D0
);

  wire and_1_out, and_2_out, and_3_out, and_4_out, and_5_out, and_6_out, and_8_out,
       bcd_to_7_segment_decoder_1_p1, bcd_to_7_segment_decoder_1_p3, bcd_to_7_segment_decoder_1_p4,
       bcd_to_7_segment_decoder_1_p5, bcd_to_7_segment_decoder_1_p6, bcd_to_7_segment_decoder_1_p8,
       bcd_to_7_segment_decoder_1_p9, bcd_to_7_segment_decoder_1_p10, bcd_to_7_segment_decoder_2_p1,
       bcd_to_7_segment_decoder_2_p2, bcd_to_7_segment_decoder_2_p3, bcd_to_7_segment_decoder_2_p4,
       bcd_to_7_segment_decoder_2_p6, bcd_to_7_segment_decoder_2_p7, bcd_to_7_segment_decoder_2_p8,
       bcd_to_7_segment_decoder_3_p1, bcd_to_7_segment_decoder_3_p2, bcd_to_7_segment_decoder_3_p3,
       bcd_to_7_segment_decoder_3_p4, bcd_to_7_segment_decoder_3_p5, bcd_to_7_segment_decoder_3_p6,
       bcd_to_7_segment_decoder_3_p7, bcd_to_7_segment_decoder_3_p8, bcd_to_7_segment_decoder_4_p1,
       bcd_to_7_segment_decoder_4_p2, bcd_to_7_segment_decoder_4_p3, bcd_to_7_segment_decoder_4_p4,
       bcd_to_7_segment_decoder_4_p5, bcd_to_7_segment_decoder_4_p6, bcd_to_7_segment_decoder_4_p7,
       bcd_to_7_segment_decoder_4_p8, Cl0ck_Button_out, fivebit_comparator_1_cout, fourbit_adder_1_c0,
       fourbit_adder_1_c1, fourbit_adder_1_c2, fourbit_adder_1_c3, fourbit_adder_1_c4, fsm_1_qq0, fsm_1_qq1,
       fsm_1_qq2, not_1_out, not_2_out, not_3_out, not_4_out, not_5_out, not_6_out, not_7_out, not_8_out,
       not_9_out, not_10_out, not_11_out, not_12_out, or_1_out, or_3_out, timer_1_timeout;
  wire [3:0] fourbit_up_counter_1_out_6, timer_1_out_5, timer_1_out_6;

  or or_1 (or_1_out, and_3_out, bcd_to_7_segment_decoder_1_p1);
  Timer timer_1 (
    .Reset(bcd_to_7_segment_decoder_1_p1), .in_3(in_1), .SET(or_1_out), .out_5(timer_1_out_5),
    .out_6(timer_1_out_6), .TIMEOUT(timer_1_timeout));  // open: in_1
  Button Cl0ck_Button (.out(Cl0ck_Button_out));
  // BCD_to_7_Segment_decoder bcd_to_7_segment_decoder_1: pin names not known; wires that end beside it: bcd_to_7_segment_decoder_1_p1, or_1_out, bcd_to_7_segment_decoder_1_p3, bcd_to_7_segment_decoder_1_p4, bcd_to_7_segment_decoder_1_p5, bcd_to_7_segment_decoder_1_p6, timer_1_out_5, bcd_to_7_segment_decoder_1_p8, bcd_to_7_segment_decoder_1_p9, bcd_to_7_segment_decoder_1_p10
  _7_Segment_Display u_7_segment_display_1 (
    .g(bcd_to_7_segment_decoder_1_p3), .f(bcd_to_7_segment_decoder_1_p5), .a(bcd_to_7_segment_decoder_1_p8),
    .b(bcd_to_7_segment_decoder_1_p10), .e(bcd_to_7_segment_decoder_1_p4), .d(bcd_to_7_segment_decoder_1_p6),
    .c(bcd_to_7_segment_decoder_1_p9));  // open: dp
  // BCD_to_7_Segment_decoder bcd_to_7_segment_decoder_2: pin names not known; wires that end beside it: bcd_to_7_segment_decoder_2_p1, bcd_to_7_segment_decoder_2_p2, bcd_to_7_segment_decoder_2_p3, bcd_to_7_segment_decoder_2_p4, timer_1_out_6, bcd_to_7_segment_decoder_2_p6, bcd_to_7_segment_decoder_2_p7, bcd_to_7_segment_decoder_2_p8
  _7_Segment_Display u_7_segment_display_2 (
    .g(bcd_to_7_segment_decoder_2_p1), .f(bcd_to_7_segment_decoder_2_p3), .a(bcd_to_7_segment_decoder_2_p6),
    .b(bcd_to_7_segment_decoder_2_p8), .e(bcd_to_7_segment_decoder_2_p2), .d(bcd_to_7_segment_decoder_2_p4),
    .c(bcd_to_7_segment_decoder_2_p7));  // open: dp
  FSM fsm_1 (
    .Cl0ck(Cl0ck_Button_out), .SS(START), .RR(RESET), .TT(timer_1_timeout), .AA(Submit), .QQ2(fsm_1_qq2),
    .QQ1(fsm_1_qq1), .QQ0(fsm_1_qq0));
  not not_1 (not_1_out, fsm_1_qq2);
  not not_2 (not_2_out, fsm_1_qq1);
  not not_3 (not_3_out, fsm_1_qq0);
  not not_4 (not_4_out, fsm_1_qq2);
  not not_5 (not_5_out, fsm_1_qq1);
  not not_6 (not_6_out, fsm_1_qq0);
  not not_7 (not_7_out, fsm_1_qq1);
  not not_8 (not_8_out, fsm_1_qq0);
  not not_9 (not_9_out, fsm_1_qq2);
  not not_10 (not_10_out, fsm_1_qq1);
  not not_11 (not_11_out, fsm_1_qq0);
  not not_12 (not_12_out, fsm_1_qq2);
  or or_2 (bcd_to_7_segment_decoder_1_p1, and_1_out, and_4_out);
  and and_1 (and_1_out, not_9_out, not_10_out, not_11_out);
  and and_2 (and_2_out, not_1_out, not_2_out, fsm_1_qq0);
  and and_3 (and_3_out, not_12_out, fsm_1_qq1, not_3_out);
  and and_4 (and_4_out, not_4_out, fsm_1_qq1, fsm_1_qq0);
  and and_5 (and_5_out, fsm_1_qq2, not_5_out, not_6_out);
  and and_6 (and_6_out, fsm_1_qq2, not_7_out, fsm_1_qq0);
  // AND_Gate and_7 has open pins: in0=fsm_1_qq2, in1=fsm_1_qq1, in2=not_8_out, out=open
  or or_3 (or_3_out, and_2_out, and_6_out);
  Randomizer randomizer_1 (.in_1(or_3_out), .out_2(C3), .out_3(C2), .out_4(C1), .out_5(C0));
  Randomizer randomizer_2 (.in_1(or_3_out), .out_2(D3), .out_3(D2), .out_4(D1), .out_5(D0));
  fourbit_adder fourbit_adder_1 (
    .A0(C3), .A1(C2), .A2(C1), .A3(C0), .B0(D3), .B1(D2), .B2(D1), .B3(D0), .C4(fourbit_adder_1_c4),
    .C3(fourbit_adder_1_c3), .C2(fourbit_adder_1_c2), .C1(fourbit_adder_1_c1), .C0(fourbit_adder_1_c0));
  fivebit_comparator fivebit_comparator_1 (
    .Check(and_4_out), .A4(A4), .B4(fourbit_adder_1_c4), .A3(A3), .B3(fourbit_adder_1_c3), .A2(A2),
    .B2(fourbit_adder_1_c2), .A1(A1), .B1(fourbit_adder_1_c1), .A0(A0), .B0(fourbit_adder_1_c0),
    .Cout(fivebit_comparator_1_cout));
  and and_8 (and_8_out, and_5_out, fivebit_comparator_1_cout);
  // BCD_to_7_Segment_decoder bcd_to_7_segment_decoder_3: pin names not known; wires that end beside it: bcd_to_7_segment_decoder_3_p1, bcd_to_7_segment_decoder_3_p2, bcd_to_7_segment_decoder_3_p3, bcd_to_7_segment_decoder_3_p4, bcd_to_7_segment_decoder_3_p5, bcd_to_7_segment_decoder_3_p6, bcd_to_7_segment_decoder_3_p7, bcd_to_7_segment_decoder_3_p8
  _7_Segment_Display u_7_segment_display_3 (
    .g(bcd_to_7_segment_decoder_3_p1), .f(bcd_to_7_segment_decoder_3_p3), .a(bcd_to_7_segment_decoder_3_p6),
    .b(bcd_to_7_segment_decoder_3_p8), .e(bcd_to_7_segment_decoder_3_p2), .d(bcd_to_7_segment_decoder_3_p4),
    .c(bcd_to_7_segment_decoder_3_p7));  // open: dp
  // BCD_to_7_Segment_decoder bcd_to_7_segment_decoder_4: pin names not known; wires that end beside it: bcd_to_7_segment_decoder_4_p1, bcd_to_7_segment_decoder_4_p2, bcd_to_7_segment_decoder_4_p3, bcd_to_7_segment_decoder_4_p4, bcd_to_7_segment_decoder_4_p5, bcd_to_7_segment_decoder_4_p6, bcd_to_7_segment_decoder_4_p7, bcd_to_7_segment_decoder_4_p8
  fourbit_up_counter fourbit_up_counter_1 (
    .in_1(and_8_out), .in_2(and_1_out), .out_3(fourbit_up_counter_1_out_6[3]),
    .out_4(fourbit_up_counter_1_out_6[2]), .out_5(fourbit_up_counter_1_out_6[1]),
    .out_6(fourbit_up_counter_1_out_6[0]));
  // Binary_to_BCD_converter #(.binvalue(4)) binary_to_bcd_converter_1: pin names not known; wires that end beside it: fourbit_up_counter_1_out_6, bcd_to_7_segment_decoder_3_p5, bcd_to_7_segment_decoder_4_p5
  _7_Segment_Display u_7_segment_display_4 (
    .g(bcd_to_7_segment_decoder_4_p1), .f(bcd_to_7_segment_decoder_4_p3), .a(bcd_to_7_segment_decoder_4_p6),
    .b(bcd_to_7_segment_decoder_4_p8), .e(bcd_to_7_segment_decoder_4_p2), .d(bcd_to_7_segment_decoder_4_p4),
    .c(bcd_to_7_segment_decoder_4_p7));  // open: dp

  // Notes on the sheet:
  //   FINITE STATE MACHINE
  //   TIMER
  //   Abhiram Suresh, 231CS202
  //   Arjun Rijesh, 231CS212
  //   Advaith Nair,231CS205
  //   QUIZ SCOREBOARD WITH TIMER
  //   INSTRUCTIONS
  //   2. Switch off Start and then press clock again, to start timer
  //   5. Press clock button again and repeat steps.
  //   1. Press Start, then the clock Button to get the random question.
  //   3. Once timer starts, you can enter answer and then switch on SUBMIT button followed by the Clock Button.
  //   4. Switch off the Submit button and then press clock button twice to compare and check the answer, which increments scoreboard by 1 if correct.
  //   SCOREBOARD
endmodule

module Randomizer (
  input  in_1,
  output out_2,
  output out_3,
  output out_4,
  output out_5
);

  wire d_ff_1_q, d_ff_2_q, d_ff_3_q, d_ff_4_q, xor_1_out;

  xor xor_1 (xor_1_out, d_ff_4_q, d_ff_1_q);
  D_Flip_Flop d_ff_1 (.D(xor_1_out), .clk(in_1), .Q(d_ff_1_q), .Qn(out_5));  // open: preset, reset
  D_Flip_Flop d_ff_2 (.D(d_ff_1_q), .clk(in_1), .Q(d_ff_2_q), .Qn(out_4));  // open: preset, reset
  D_Flip_Flop d_ff_3 (.D(d_ff_2_q), .clk(in_1), .Q(d_ff_3_q), .Qn(out_3));  // open: preset, reset
  D_Flip_Flop d_ff_4 (.D(d_ff_3_q), .clk(in_1), .Q(d_ff_4_q), .Qn(out_2));  // open: preset, reset
endmodule

module full_adder (
  input  A,
  input  B,
  input  Cin,
  output Sum,
  output Cout
);

  wire and_1_out, and_2_out, xor_1_out;

  xor xor_1 (xor_1_out, A, B);
  and and_1 (and_1_out, A, B);
  xor xor_2 (Sum, xor_1_out, Cin);
  and and_2 (and_2_out, xor_1_out, Cin);
  or or_1 (Cout, and_1_out, and_2_out);
endmodule

module fourbit_adder (
  input  A0,
  input  A1,
  input  A2,
  input  A3,
  input  B0,
  input  B1,
  input  B2,
  input  B3,
  output C4,
  output C3,
  output C2,
  output C1,
  output C0
);

  wire full_adder_1_cout, full_adder_2_cout, full_adder_3_cout, undriven;

  full_adder full_adder_1 (.A(A0), .B(B0), .Cin(undriven), .Sum(C1), .Cout(full_adder_1_cout));
  full_adder full_adder_2 (.A(A1), .B(B1), .Cin(full_adder_1_cout), .Sum(C0), .Cout(full_adder_2_cout));
  full_adder full_adder_3 (.A(A2), .B(B2), .Cin(full_adder_2_cout), .Sum(C2), .Cout(full_adder_3_cout));
  full_adder full_adder_4 (.A(A3), .B(B3), .Cin(full_adder_3_cout), .Sum(C3), .Cout(C4));
endmodule

module fourbit_subtractor (
  input  A0,
  input  A1,
  input  A2,
  input  A3,
  input  B0,
  input  B1,
  input  B2,
  input  B3,
  output out_9,
  output out_10,
  output out_11,
  output out_12,
  output out_13
);

  wire full_adder_1_cout, full_adder_1_sum, full_adder_2_cout, full_adder_2_sum, full_adder_3_cout,
       full_adder_3_sum, full_adder_4_cout, full_adder_4_sum, full_adder_5_cout, full_adder_6_cout,
       full_adder_7_cout, full_adder_8_cout, not_1_out, not_2_out, undriven, xor_1_out, xor_2_out, xor_3_out,
       xor_4_out;

  full_adder full_adder_1 (.A(A0), .B(B0), .Cin(undriven), .Sum(full_adder_1_sum), .Cout(full_adder_1_cout));
  full_adder full_adder_2 (.A(A1), .B(B1), .Cin(full_adder_1_cout), .Sum(full_adder_2_sum), .Cout(full_adder_2_cout));
  full_adder full_adder_3 (.A(A2), .B(B2), .Cin(full_adder_2_cout), .Sum(full_adder_3_sum), .Cout(full_adder_3_cout));
  xor xor_1 (xor_1_out, out_13, full_adder_1_sum);
  not not_1 (not_1_out, out_13);
  full_adder full_adder_4 (.A(A3), .B(B3), .Cin(full_adder_3_cout), .Sum(full_adder_4_sum), .Cout(full_adder_4_cout));
  not not_2 (not_2_out, full_adder_4_cout);
  and and_1 (out_13, not_2_out, 1'b1);
  full_adder full_adder_5 (.B(xor_1_out), .Cin(not_1_out), .Sum(out_12), .Cout(full_adder_5_cout));  // open: A
  xor xor_2 (xor_2_out, out_13, full_adder_2_sum);
  full_adder full_adder_6 (.B(xor_2_out), .Cin(full_adder_5_cout), .Sum(out_11), .Cout(full_adder_6_cout));  // open: A
  xor xor_3 (xor_3_out, out_13, full_adder_3_sum);
  full_adder full_adder_7 (.B(xor_3_out), .Cin(full_adder_6_cout), .Sum(out_10), .Cout(full_adder_7_cout));  // open: A
  xor xor_4 (xor_4_out, full_adder_4_sum, out_13);
  full_adder full_adder_8 (.B(xor_4_out), .Cin(full_adder_7_cout), .Sum(out_9), .Cout(full_adder_8_cout));  // open: A
endmodule

module fivebit_comparator (
  input  Check,
  input  A4,
  input  B4,
  input  A3,
  input  B3,
  input  A2,
  input  B2,
  input  A1,
  input  B1,
  input  A0,
  input  B0,
  output Cout
);

  wire xnor_1_out, xnor_2_out, xnor_3_out, xnor_4_out, xnor_5_out;

  xnor xnor_1 (xnor_1_out, A4, B4);
  xnor xnor_2 (xnor_2_out, A3, B3);
  xnor xnor_3 (xnor_3_out, A2, B2);
  xnor xnor_4 (xnor_4_out, A1, B1);
  xnor xnor_5 (xnor_5_out, A0, B0);
  and and_1 (Cout, Check, xnor_1_out, xnor_2_out, xnor_3_out, xnor_4_out, xnor_5_out);
endmodule

module fourbit_up_counter (
  input  in_1,
  input  in_2,
  output out_3,
  output out_4,
  output out_5,
  output out_6
);

  wire undriven;

  T_Flip_Flop #(.trigger("falling")) t_ff_1 (.T(1'b1), .clk(in_1), .Q(out_6), .reset(in_2));  // open: Qn, preset
  T_Flip_Flop #(.trigger("falling")) t_ff_2 (
    .T(1'b1), .clk(out_6), .Q(out_5), .reset(in_2), .preset(undriven));  // open: Qn
  T_Flip_Flop #(.trigger("falling")) t_ff_3 (.T(1'b1), .clk(out_5), .Q(out_4), .reset(in_2));  // open: Qn, preset
  T_Flip_Flop #(.trigger("falling")) t_ff_4 (.T(1'b1), .clk(out_4), .Q(out_3), .reset(in_2));  // open: Qn, preset
endmodule

module is_subtractor (
  input  in_1,
  input  in_2,
  input  in_3,
  input  in_4,
  input  in_5,
  input  in_6,
  input  in_7,
  input  in_8
);

  // XOR_Gate xor_1 has open pins: in0=1'b1, in1=in_1, out=open
  // XOR_Gate xor_2 has open pins: in0=1'b1, in1=in_2, out=open
  // XOR_Gate xor_3 has open pins: in0=1'b1, in1=in_3, out=open
  // XOR_Gate xor_4 has open pins: in0=1'b1, in1=in_4, out=open
  // XOR_Gate xor_5 has open pins: in0=1'b1, in1=in_5, out=open
  // XOR_Gate xor_6 has open pins: in0=1'b1, in1=in_6, out=open
  // XOR_Gate xor_7 has open pins: in0=1'b1, in1=in_7, out=open
  // XOR_Gate xor_8 has open pins: in0=1'b1, in1=in_8, out=open
endmodule

module FSM (
  input  Cl0ck,
  input  SS,
  input  RR,
  input  TT,
  input  AA,
  output QQ2,
  output QQ1,
  output QQ0
);

  wire and_1_out, and_2_out, and_3_out, and_4_out, not_1_out, not_2_out, not_3_out, or_1_out, or_2_out,
       or_3_out, Q0_qn, Q1_qn, Q2_qn;

  D_Flip_Flop Q2 (.D(or_3_out), .clk(Cl0ck), .Q(QQ2), .Qn(Q2_qn));  // open: preset, reset
  D_Flip_Flop Q1 (.D(or_2_out), .clk(Cl0ck), .Q(QQ1), .Qn(Q1_qn));  // open: preset, reset
  D_Flip_Flop Q0 (.D(or_1_out), .clk(Cl0ck), .Q(QQ0), .Qn(Q0_qn));  // open: preset, reset
  not not_1 (not_1_out, RR);
  not not_2 (not_2_out, RR);
  and and_1 (and_1_out, QQ2, Q1_qn, not_1_out);
  and and_2 (and_2_out, not_1_out, QQ0, Q1_qn);
  and and_3 (and_3_out, not_2_out, QQ0, QQ1);
  or or_1 (or_1_out, and_1_out, SS, AA, TT);
  not not_3 (not_3_out, TT);
  and and_4 (and_4_out, not_3_out, not_1_out, Q0_qn, QQ1, Q2_qn);
  or or_2 (or_2_out, and_4_out, and_2_out);
  or or_3 (or_3_out, and_3_out, TT);
endmodule

module Timer (
  input  in_1,
  input  Reset,
  input  in_3,
  input  SET,
  output [3:0] out_5,
  output [3:0] out_6,
  output TIMEOUT
);

  wire and_1_out, CL0CK_out;
  wire [3:0] counter_1_q;

  Clock CL0CK (.out(CL0CK_out));
  and and_1 (and_1_out, CL0CK_out, SET);
  Counter #(.max('hf), .width(4)) counter_1 (
    .clr(in_1), .load(Reset), .up(in_3), .clk(and_1_out), .carry(TIMEOUT), .Q(counter_1_q));  // open: count, D
  // Binary_to_BCD_converter #(.binvalue(4)) binary_to_bcd_converter_1: pin names not known; wires that end beside it: counter_1_q, out_5, out_6
endmodule
